# Fritzing sketch MyLifeIsPatate (saved by Fritzing 0.9.2b)
breadboards: 1

parts:
  Composant1 = Arduino BT
  R1 = Resistor [tolerance=±5% resistance=10k package="0805 [SMD]"]
  C1 = Ceramic Capacitor [capacitance=10nF package="1206 [SMD, multilayer]"]
  L1 = Inductor [package="0603 [SMD]"]
  R2 = Resistor [tolerance=±5% resistance=1M package="0805 [SMD]"]
  LED1 = LED - 5mm [color="Red (633nm)" package="5 mm [THT]"]
  R3 = Resistor [tolerance=±5% resistance=3.3k package="0805 [SMD]"]
  C2 = Ceramic Capacitor [capacitance=0.1nF package="1206 [SMD, multilayer]"]

nets:
  N1: Composant1.PWM_D9, R1.Pin_0
  N2: Composant1.A0, R2.Pin_0, LED1.cathode, C2.0
  N3: Composant1.GND, R2.Pin_1, R3.Pin_0, C2.1
  N4: R1.Pin_1, L1.pin_0, R3.Pin_1
  N5: C1.0, L1.pin_1, LED1.anode
